// Logisim project 16bit register.circ as structural Verilog: 2 circuits, main circuit main
// Value Reg1
module main (
  input  [3:0] Read_Reg2,
  input  [3:0] Read_Reg1,
  input  [15:0] Data,
  input  [3:0] Write_Reg,
  input  Write,
  input  Clock,
  input  Reset_Clear,
  output [15:0] Value_Reg2,
  output [15:0] Value_Reg1
);

  wire decoder_1_out0, decoder_1_out1, decoder_1_out2, decoder_1_out3, decoder_1_out4, decoder_1_out5,
       decoder_1_out6, decoder_1_out7, decoder_1_out8, decoder_1_out9, decoder_1_out10, decoder_1_out11,
       decoder_1_out12, decoder_1_out13, decoder_1_out14, decoder_1_out15;
  wire [15:0] R1_q, R2_q, register_1_q, register_2_q, register_3_q, register_4_q, register_5_q, register_6_q,
       register_7_q, register_8_q, register_9_q, register_10_q, register_11_q, register_12_q, register_13_q,
       register_14_q;

  Decoder #(.select(4), .disabled(0)) decoder_1 (
    .out0(decoder_1_out0), .out1(decoder_1_out1), .out2(decoder_1_out2), .out3(decoder_1_out3),
    .out4(decoder_1_out4), .out5(decoder_1_out5), .out6(decoder_1_out6), .out7(decoder_1_out7),
    .out8(decoder_1_out8), .out9(decoder_1_out9), .out10(decoder_1_out10), .out11(decoder_1_out11),
    .out12(decoder_1_out12), .out13(decoder_1_out13), .out14(decoder_1_out14), .out15(decoder_1_out15),
    .sel(Write_Reg), .en(Write));
  Register #(.width(16), .trigger("falling")) R1 (
    .D(Data), .en(decoder_1_out0), .Q(R1_q), .clk(Clock), .clr(Reset_Clear));
  Register #(.width(16), .trigger("falling")) R2 (
    .D(Data), .en(decoder_1_out1), .Q(R2_q), .clk(Clock), .clr(Reset_Clear));
  Register #(.width(16), .trigger("falling")) register_1 (
    .D(Data), .en(decoder_1_out2), .Q(register_1_q), .clk(Clock), .clr(Reset_Clear));
  Register #(.width(16), .trigger("falling")) register_2 (
    .D(Data), .en(decoder_1_out3), .Q(register_2_q), .clk(Clock), .clr(Reset_Clear));
  Register #(.width(16), .trigger("falling")) register_3 (
    .D(Data), .en(decoder_1_out4), .Q(register_3_q), .clk(Clock), .clr(Reset_Clear));
  Register #(.width(16), .trigger("falling")) register_4 (
    .D(Data), .en(decoder_1_out5), .Q(register_4_q), .clk(Clock), .clr(Reset_Clear));
  Register #(.width(16), .trigger("falling")) register_5 (
    .D(Data), .en(decoder_1_out6), .Q(register_5_q), .clk(Clock), .clr(Reset_Clear));
  Register #(.width(16), .trigger("falling")) register_6 (
    .D(Data), .en(decoder_1_out7), .Q(register_6_q), .clk(Clock), .clr(Reset_Clear));
  Register #(.width(16), .trigger("falling")) register_7 (
    .D(Data), .en(decoder_1_out8), .Q(register_7_q), .clk(Clock), .clr(Reset_Clear));
  Register #(.width(16), .trigger("falling")) register_8 (
    .D(Data), .en(decoder_1_out9), .Q(register_8_q), .clk(Clock), .clr(Reset_Clear));
  Register #(.width(16), .trigger("falling")) register_9 (
    .D(Data), .en(decoder_1_out10), .Q(register_9_q), .clk(Clock), .clr(Reset_Clear));
  Register #(.width(16), .trigger("falling")) register_10 (
    .D(Data), .en(decoder_1_out11), .Q(register_10_q), .clk(Clock), .clr(Reset_Clear));
  Register #(.width(16), .trigger("falling")) register_11 (
    .D(Data), .en(decoder_1_out12), .Q(register_11_q), .clk(Clock), .clr(Reset_Clear));
  Register #(.width(16), .trigger("falling")) register_12 (
    .D(Data), .en(decoder_1_out13), .Q(register_12_q), .clk(Clock), .clr(Reset_Clear));
  Register #(.width(16), .trigger("falling")) register_13 (
    .D(Data), .en(decoder_1_out14), .Q(register_13_q), .clk(Clock), .clr(Reset_Clear));
  Register #(.width(16), .trigger("falling")) register_14 (
    .D(Data), .en(decoder_1_out15), .Q(register_14_q), .clk(Clock), .clr(Reset_Clear));
  Multiplexer #(.select(4), .width(16), .enable("false")) multiplexer_1 (
    .in0(R1_q), .in1(R2_q), .in2(register_1_q), .in3(register_2_q), .in4(register_3_q), .in5(register_4_q),
    .in6(register_5_q), .in7(register_6_q), .in8(register_7_q), .in9(register_8_q), .in10(register_9_q),
    .in11(register_10_q), .in12(register_11_q), .in13(register_12_q), .in14(register_13_q),
    .in15(register_14_q), .out(Value_Reg1), .sel(Read_Reg1));
  Multiplexer #(.select(4), .width(16), .enable("false")) multiplexer_2 (
    .in0(R1_q), .in1(R2_q), .in2(register_1_q), .in3(register_2_q), .in4(register_3_q), .in5(register_4_q),
    .in6(register_5_q), .in7(register_6_q), .in8(register_7_q), .in9(register_8_q), .in10(register_9_q),
    .in11(register_10_q), .in12(register_11_q), .in13(register_12_q), .in14(register_13_q),
    .in15(register_14_q), .out(Value_Reg2), .sel(Read_Reg2));
endmodule

module _16_bit_read_write_reg (
  input  [3:0] Write_Reg,
  input  [15:0] Data,
  input  [3:0] Read_Reg2,
  input  [3:0] Read_Reg1,
  input  write,
  input  clear,
  output [15:0] Value_Reg2,
  output [15:0] Value_Reg1
);

  wire main_1_p7;

  // main main_1: pin names not known; wires that end beside it: Value_Reg2, Value_Reg1, Read_Reg2, Read_Reg1, Write_Reg, write, main_1_p7, Data, clear
  Clock Clock (.out(main_1_p7));
endmodule
